# Fritzing sketch Schematics (saved by Fritzing 0.9.3b)
breadboards: 1

parts:
  C1 = Electrolytic Capacitor [capacitance=1mF package="0807 [SMD, electrolytic]"]
  R1 = Resistor [tolerance=±5% resistance=330 package=THT]
  NEOPIXEL1 = Neopixel Strip -- Black (30/m)
  Part1 = SparkFun ESP8266 Thing
  X2 = USB Connectors [package=usb-a-s-silk-female]
  SparkFun_ESP32_Thing1 = SparkFun ESP32 Thing [part_number=DEV-13907]  # not connected

nets:
  GND: C1.-, NEOPIXEL1.GND, Part1.GND, X2.GND
  N1: C1.+, NEOPIXEL1.+5V, X2.VBUS
  N2: R1.Pin_0, NEOPIXEL1.DI
  N3: R1.Pin_1, Part1.GPIO13

custom parts:
  Neopixel Strip -- Black (30/m): Neopixel Strip, Black, 30 pixels per meter.
  SparkFun ESP32 Thing: The SparkFun ESP32 Thing is a comprehensive development platform for Espressif’s ESP32, their super-charged version of the popular ESP8266. Like the 8266, the ESP32 is a WiFi-compatible microcontroller, but to that it adds support for Bluetooth low-energy (i.e BLE, BT4.0, Bluetooth Smart), and nearly 30 I/O pins. The ESP32’s power and versatility will make it the foundation of IoT and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
